// Logisim project ex0.circ as structural Verilog: 1 circuit, main circuit main
module main (
  input  First_Input_Pin,
  input  Second_Input_Pin,
  output Output_Pin
);


  // Notes on the sheet:
  //   AND Gate
  //   Note
  //   Please, do not modify/change/replace the input and output pins
endmodule
