// Logisim project ex1.circ as structural Verilog: 5 circuits, main circuit NAND
module NAND (
  input  First_Input_Pin,
  input  Second_Input_Pin,
  output Output_Pin
);


  // Notes on the sheet:
  //   Your Circuit Here
  //   Note
  //   Please, do not modify/change/replace the input and output pins
endmodule

module NOR (
  input  First_Input_Pin,
  input  Second_Input_Pin,
  output Output_Pin
);


  // Notes on the sheet:
  //   Your Circuit Here
  //   Note
  //   Please, do not modify/change/replace the input and output pins
endmodule

module XOR (
  input  First_Input_Pin,
  input  Second_Input_Pin,
  output Output_Pin
);


  // Notes on the sheet:
  //   Your Circuit Here
  //   Note
  //   Please, do not modify/change/replace the input and output pins
endmodule

module _2_1MUX (
  input  x,
  input  y,
  input  s0,
  output out
);


  // Notes on the sheet:
  //   Inputs
  //   Your Circuit Here
  //   Selector
  //   Note
  //   Please, do not modify/change/replace the input and output pins
  //   Output Pin
endmodule

module _4_1MUX (
  input  x,
  input  y,
  input  z,
  input  w,
  input  s1,
  input  s0,
  output out
);


  // Notes on the sheet:
  //   Inputs
  //   Your Circuit Here
  //   Selector
  //   Note
  //   Please, do not modify/change/replace the input and output pins
  //   Output Pin
endmodule
