// Logisim project ex2.circ as structural Verilog: 1 circuit, main circuit main
module main (
  output [7:0] X_1,
  output [7:0] X
);


  // Notes on the sheet:
  //   Your circuit here
  //   Note
  //   Please, do not modify/change/replace the output pins
  //   Outputs
endmodule
