// Logisim project ex3.circ as structural Verilog: 4 circuits, main circuit AFD
module AFD (
  input  AFD_Input,
  input  [1:0] State,
  output AFD_Output,
  output [1:0] NewState
);

  AFDLogic afdlogic_1 (.Input(AFD_Input), .Current_State(State), .Output(AFD_Output), .Next_State(NewState));

  // Notes on the sheet:
  //   Note
  //   Please, do not modify this circuit
endmodule

// AFD Logic
module AFDLogic (
  input  Input,
  input  [1:0] Current_State,
  output Output,
  output [1:0] Next_State
);

  wire and_1_out, and_2_out, not_1_out, not_2_out, not_3_out;

  not not_1 (not_1_out, Input);
  not not_2 (not_2_out, Current_State[0]);
  not not_3 (not_3_out, Current_State[1]);
  and and_1 (and_1_out, Input, not_3_out);
  and and_2 (and_2_out, not_1_out, not_2_out);
  StateBitZero statebitzero_1 (
    .Input(Input), .State_Bit_0(Current_State[0]), .State_Bit_1(Current_State[1]), .New_State_0(Next_State[0]));
  StateBitOne statebitone_1 (
    .Input(Input), .New_State_1(Next_State[1]), .State_Bit_0(Current_State[0]), .State_Bit_1(Current_State[1]));
  or or_1 (Output, and_1_out, and_2_out);

  // Notes on the sheet:
  //   Note
  //   Please, do not modify this circuit
endmodule

// Stat Bit 1
module StateBitOne (
  input  Input,
  input  State_Bit_0,
  input  State_Bit_1,
  output New_State_1
);


  // Notes on the sheet:
  //   Inputs
  //   Your Circuit Here
  //   Note
  //   Please, do not modify/change/replace the output and input pins
  //   Output
endmodule

// State Bit 0
module StateBitZero (
  input  Input,
  input  State_Bit_0,
  input  State_Bit_1,
  output New_State_0
);


  // Notes on the sheet:
  //   Inputs
  //   Your Circuit Here
  //   Note
  //   Please, do not modify/change/replace the output and input pins
  //   Output
endmodule
