// Logisim project ex0.circ as structural Verilog: 1 circuit, main circuit main
module main (
  output out_1,
  output out_2,
  output out_3,
  output halt
);

  wire clock_1_out;
  wire [7:0] adder_1_out, cnt;

  Register register_1 (.D(adder_1_out), .Q(cnt), .clk(clock_1_out));  // open: en, clr
  Clock clock_1 (.out(clock_1_out));
  Adder adder_1 (.a(8'h1), .b(cnt), .out(adder_1_out));  // open: cin, cout
  ex0_main main_1 (.First_Input_Pin(out_1), .Second_Input_Pin(out_2), .Output_Pin(out_3));
  ROM #(.dataWidth(2)) rom_1 (.addr(cnt), .data({out_1, out_2}), .sel(1'b1));
  Comparator #(.mode("unsigned")) comparator_1 (.a(8'h3), .b(cnt), .eq(halt));  // open: gt, lt

  // Other names for the same wires on the sheet: B = out_2; A = out_1; C = out_3

  // Notes on the sheet:
  //   Output
  //   Counter
  //   Tests
  //   contents of rom_1 (hex, n*v repeats v):
  //   0 1 2 3
  //   Halt signal
  //   Note
  //   Please, do not modify this file
endmodule
