// Logisim project ex1.circ as structural Verilog: 1 circuit, main circuit main
module main (
  output [4:0] out_1,
  output [3:0] out_2,
  output [6:0] out_3,
  output halt
);

  wire clock_1_out;
  wire [7:0] adder_1_out, cnt;

  Register register_1 (.D(adder_1_out), .Q(cnt), .clk(clock_1_out));  // open: en, clr
  Clock clock_1 (.out(clock_1_out));
  Adder adder_1 (.a(8'h1), .b(cnt), .out(adder_1_out));  // open: cin, cout
  NAND nand_1 (.First_Input_Pin(out_1[4]), .Second_Input_Pin(out_1[3]), .Output_Pin(out_1[2]));
  NOR nor_1 (.First_Input_Pin(out_1[4]), .Second_Input_Pin(out_1[3]), .Output_Pin(out_1[1]));
  XOR xor_1 (.First_Input_Pin(out_1[4]), .Second_Input_Pin(out_1[3]), .Output_Pin(out_1[0]));
  _2_1MUX u_2_1mux_1 (.x(out_2[3]), .y(out_2[2]), .out(out_2[0]), .s0(out_2[1]));
  ROM #(.dataWidth(2)) rom_1 (.addr(cnt), .data(out_1[4:3]), .sel(1'b1));
  _4_1MUX u_4_1mux_1 (
    .x(out_3[6]), .y(out_3[5]), .z(out_3[4]), .w(out_3[3]), .out(out_3[0]), .s1(out_3[1]), .s0(out_3[2]));
  ROM #(.dataWidth(3)) rom_2 (.addr(cnt), .data(out_2[3:1]), .sel(1'b1));
  Comparator #(.mode("unsigned")) comparator_1 (.a(8'h3f), .b(cnt), .eq(halt));  // open: gt, lt
  ROM #(.dataWidth(6)) rom_3 (.addr(cnt), .data({out_3[6:3], out_3[1], out_3[2]}), .sel(1'b1));

  // Other names for the same wires on the sheet: O3 = out_1[0]; O2 = out_1[1]; O1 = out_1[2]; B = out_1[3];
  //   A = out_1[4]; O4 = out_2[0]; s0 = out_2[1]; y0 = out_2[2]; x0 = out_2[3]; O5 = out_3[0]; s2 = out_3[1];
  //   s1 = out_3[2]; w1 = out_3[3]; z1 = out_3[4]; y1 = out_3[5]; x1 = out_3[6]

  // Notes on the sheet:
  //   Counter
  //   Gates Outputs
  //   GatesTests
  //   2-1 Output
  //   contents of rom_1 (hex, n*v repeats v):
  //   0 1 2 3
  //   4-1 Output
  //   Note
  //   Please, do not modify this file
  //   2-1 Tests
  //   contents of rom_2 (hex, n*v repeats v):
  //   0 1 2 3 4 5 6 7
  //   Halt signal
  //   4-1 Tests
  //   contents of rom_3 (hex, n*v repeats v):
  //   0 1 2 3 4 5 6 7 8 9 a b c d e f 10 11 12 13 14 15 16 17 18 19 1a 1b 1c 1d 1e 1f 20 21 22 23 24 25 26
  //   27 28 29 2a 2b 2c 2d 2e 2f 30 31 32 33 34 35 36 37 38 39 3a 3b 3c 3d 3e 3f
endmodule
