// Logisim project ex2.circ as structural Verilog: 1 circuit, main circuit main
module main (
  output halt,
  output [7:0] out_2,
  output [7:0] out_3
);

  wire clock_1_out;
  wire [7:0] adder_1_out, cnt;

  Register register_1 (.D(adder_1_out), .Q(cnt), .clk(clock_1_out));  // open: en, clr
  Clock clock_1 (.out(clock_1_out));
  Adder adder_1 (.a(8'h1), .b(cnt), .out(adder_1_out));  // open: cin, cout
  Comparator #(.mode("unsigned")) comparator_1 (.a({8{1'b1}}), .b(cnt), .eq(halt));  // open: gt, lt
  ex2_main main_1 (.X_1(out_3), .X(out_2));

  // Other names for the same wires on the sheet: O0[7:0] = out_2; O1[7:0] = out_3

  // Notes on the sheet:
  //   Counter
  //   Halt signal
  //   Output
  //   Note
  //   Please, do not modify this file
endmodule
