// Logisim project ex3.circ as structural Verilog: 1 circuit, main circuit main
module main (
  output halt,
  output [2:0] out_2,
  output [2:0] out_3
);

  wire clock_1_out;
  wire [7:0] adder_1_out, cnt;

  Register register_1 (.D(adder_1_out), .Q(cnt), .clk(clock_1_out));  // open: en, clr
  Clock clock_1 (.out(clock_1_out));
  Adder adder_1 (.a(8'h1), .b(cnt), .out(adder_1_out));  // open: cin, cout
  Comparator #(.mode("unsigned")) comparator_1 (.a(8'h7), .b(cnt), .eq(halt));  // open: gt, lt
  ROM #(.dataWidth(3)) rom_1 (.addr(cnt), .data(out_2), .sel(1'b1));
  AFD afd_1 (.AFD_Input(out_2[0]), .State(out_2[2:1]), .NewState(out_3[2:1]), .AFD_Output(out_3[0]));

  // Other names for the same wires on the sheet: I = out_2[0]; O1[2:0] = out_2; S[1:0] = out_2[2:1]; O2[2:0] = out_3

  // Notes on the sheet:
  //   Counter
  //   Halt signal
  //   Tests
  //   Note
  //   Please, do not modify this file
  //   contents of rom_1 (hex, n*v repeats v):
  //   0 1 2 3 4 5 6 7
  //   Output
endmodule
